// Logisim project Inst_memory.circ as structural Verilog
module main (
  input  [19:0] in_1,
  output [31:0] out_2
);

  ROM #(.addrWidth(20), .dataWidth(32)) rom_1 (.addr(in_1), .data(out_2));

  // Other names for the same wires on the sheet: instruction[31:0] = out_2; PC[19:0] = in_1
endmodule
